# Fritzing sketch implementação (saved by Fritzing 1.0.1rc)
breadboards: 1

parts:
  Nano1 = Arduino Nano v2.3
  IR1 = vs1838b [package=THT]

nets:
  GND: Nano1.GND, IR1.GND
  N1: Nano1.D2, IR1.Data
  N2: Nano1.+5V, IR1.Vs
