# Fritzing sketch parte2 (saved by Fritzing 1.0.1rc)
breadboards: 1

parts:
  VCC1 = Battery block 9V
  Nano1 = Arduino Nano v2.3
  Part1 = Bluetooth HC-05 Macho
  Part2 = Logic Level Converter
  D1 = LTE-302 [package=lte-302]
  R1 = Resistor [tolerance=±5% resistance=220 package="0805 [SMD]"]

nets:
  N1: VCC1.-, Nano1.GND, R1.Pin_1
  N2: Nano1.D3, D1.A
  N3: Nano1.D10, Part1.TXD
  N4: Nano1.D11, Part2.RX2_HV
  N5: Nano1.3V3, Part2.LV
  +5V: Nano1.+5V, Part1.VCC, Part2.HV
  GND: Nano1.VIN, Part1.GND, Part2.GND
  N6: Part1.RXD, Part2.RX2_LV
  N7: D1.C, R1.Pin_0
